// Logisim project HW3.circ as structural Verilog
module cpu_main (
  input  in_1,
  input  in_2,
  input  in_3,
  input  in_4,
  input  in_5,
  input  in_6,
  input  in_7,
  input  [15:0] in_8,
  input  [15:0] in_9,
  input  [15:0] in_10,
  input  [15:0] in_11,
  input  [3:0] in_12,
  output [5:0] out_13,
  output [15:0] out_14,
  output [15:0] out_15,
  output [3:0] out_16,
  output [2:0] out_17,
  output [15:0] out_18,
  output [2:0] out_19,
  output [4:0] out_20,
  output [3:0] out_21,
  output [15:0] out_22,
  output [15:0] out_23,
  output [11:0] out_24
);

  wire and_3_out, ble, clock, clock_1_out, comparator_1_lt, control_1_load_cmd, control_1_out_3,
       control_1_shut_down_halt, control_1_store_cmd, control_1_write, I_R, if_call, if_jump, if_rtn,
       multiplexer_4_out, not_1_out, not_2_out, not_3_out, or_1_out;
  wire [1:0] negator_1_out;
  wire [5:0] negator_3_out;
  wire [15:0] adder_2_out, ALUout, bit_extender_1_out, bit_extender_2_out, bit_extender_3_out,
       bit_extender_4_out, dataMem, Jump_x, multiplexer_1_out, multiplexer_2_out, multiplexer_3_out,
       multiplexer_5_out, multiplexer_6_out, multiplexer_7_out, negator_4_out, pc_adder, r1_data, r2_data,
       ra_data, register_1_q;
  wire [15:11] ram_1_data;

  Clock clock_1 (.out(clock_1_out));
  Multiplexer #(.width(16)) multiplexer_1 (
    .in0(pc_adder), .in1(ra_data), .out(multiplexer_1_out), .sel(if_rtn));  // open: en
  and and_1 (clock, clock_1_out, not_1_out);
  not not_1 (not_1_out, control_1_shut_down_halt);
  Multiplexer #(.width(16)) multiplexer_2 (
    .in0(16'h1), .in1(out_14), .out(multiplexer_2_out), .sel(and_3_out));  // open: en
  Register #(.width(16)) register_1 (.D(multiplexer_1_out), .en(1'b1), .Q(register_1_q), .clk(clock));  // open: clr
  assign out_22 = in_8 & in_11;  // AND_Gate and_2, 16 bits wide
  Multiplexer #(.width(16)) multiplexer_3 (
    .in0(multiplexer_2_out), .in1(Jump_x), .out(multiplexer_3_out), .sel(if_jump));  // open: en
  and and_3 (and_3_out, comparator_1_lt, ble);
  Comparator #(.width(16)) comparator_1 (.a(r1_data), .b(r2_data), .lt(comparator_1_lt));  // open: gt, eq
  Adder #(.width(16)) adder_1 (.a(multiplexer_3_out), .b(register_1_q), .out(pc_adder));  // open: cin, cout
  RAM #(.addrWidth(16), .dataWidth(16), .bus("separate")) ram_1 (
    .addr(register_1_q), .data({ram_1_data, out_13, out_19, out_20[1:0]}), .sel(1'b1), .ld(1'b1));  // open: din, str, clk, clr
  Multiplexer multiplexer_4 (.in0(in_2), .in1(in_4), .out(multiplexer_4_out), .sel(in_6));  // open: en
  Negator #(.width(2)) negator_1 (.in(out_20[1:0]), .out(negator_1_out));
  control control_1 (
    .opcode(ram_1_data), .shut_down_halt(control_1_shut_down_halt), .write(control_1_write), .I_or_R(I_R),
    .out_3(control_1_out_3), .BLE(ble), .load_cmd(control_1_load_cmd), .store_cmd(control_1_store_cmd),
    .jump_cmd(if_jump), .call(if_call), .rtn(if_rtn));
  Shifter #(.width(16)) shifter_1 (.in(in_9), .\dist (in_12), .out(out_23));
  Adder #(.width(16)) adder_2 (.a(16'h1), .b(register_1_q), .out(adder_2_out));  // open: cin, cout
  assign bit_extender_1_out = {{14{1'b0}}, negator_1_out};  // Bit_Extender bit_extender_1
  assign bit_extender_2_out = {{11{1'b0}}, {out_19, out_20[1:0]}};  // Bit_Extender bit_extender_2
  Negator #(.width(16)) negator_2 (.in(bit_extender_1_out), .out(out_14));
  Multiplexer #(.width(16)) multiplexer_5 (
    .in0(r2_data), .in1(bit_extender_2_out), .out(multiplexer_5_out), .sel(not_3_out));  // open: en
  Multiplexer #(.width(16)) multiplexer_6 (
    .in0(bit_extender_2_out), .in1(dataMem), .out(multiplexer_6_out), .sel(control_1_load_cmd));  // open: en
  or or_1 (or_1_out, control_1_out_3, control_1_load_cmd);
  not not_2 (not_2_out, or_1_out);
  Register #(.width(16)) register_2 (.D(adder_2_out), .en(if_call), .Q(ra_data), .clk(clock));  // open: clr
  not not_3 (not_3_out, I_R);
  Multiplexer #(.width(16)) multiplexer_7 (
    .in0(multiplexer_6_out), .in1(ALUout), .out(multiplexer_7_out), .sel(not_2_out));  // open: en
  ALU alu_1 (
    .op1(r1_data), .op2(multiplexer_5_out), .opcode_decide_which_instrusion_would_be_selected(ram_1_data),
    .data_output(ALUout));
  register register_3 (
    .allow_write(control_1_write), .Write_Register_which_reg(out_13[5:3]),
    .Register_Data_data_input(multiplexer_7_out), .clock_update_reg_per_clock(clock), .data_1(r1_data),
    .data_2(r2_data), .Read_Regisiter2(out_19), .Read_Regisiter1(out_13[2:0]));  // open: reset
  assign bit_extender_3_out = {{10{1'b0}}, out_13};  // Bit_Extender bit_extender_3
  Negator #(.width(6)) negator_3 (.in(out_13), .out(negator_3_out));
  assign bit_extender_4_out = {{10{1'b0}}, negator_3_out};  // Bit_Extender bit_extender_4
  Negator #(.width(16)) negator_4 (.in(bit_extender_4_out), .out(negator_4_out));
  RAM #(.addrWidth(16), .dataWidth(16), .bus("separate")) ram_2 (
    .addr(r1_data), .din(r2_data), .data(dataMem), .str(control_1_store_cmd), .sel(1'b1), .clk(clock),
    .ld(control_1_load_cmd));  // open: clr
  Multiplexer #(.width(16)) multiplexer_8 (
    .in0(bit_extender_3_out), .in1(negator_4_out), .out(Jump_x), .sel(out_13[5]));  // open: en

  assign out_16 = {in_7, in_5, in_3, in_1};
  assign out_17 = out_13[5:3];
  assign out_20[4:2] = out_19;
  assign out_21 = in_10[3:0];
  assign out_24 = in_10[15:4];

  // Other names for the same wires on the sheet: ble2[15:0] = out_14; debug1[15:0] = out_18;
  //   ime[4:0] = {out_19, out_20[1:0]}; r2[2:0] = out_19; ime_data[15:0] = out_15; Jnum[5:0] = out_13;
  //   r1[2:0] = out_13[2:0]; des[2:0] = out_13[5:3]; J_neg = out_13[5]

  // Notes on the sheet:
  //   program counter
  //   if ble
  //   debug area
  //   BLE
  //   debug area
  //   ra reg
  //   debug area
  //   J type ime number
  //   data memory
endmodule

module ALU (
  input  [15:0] op1,
  input  [15:0] op2,
  input  [4:0] opcode_decide_which_instrusion_would_be_selected,
  output [15:0] data_output
);

  wire adder_2_cout, comparator_1_lt, comparator_2_gt;
  wire [15:0] adder_1_out, adder_2_out, adder_3_out, and_1_out, and_2_out, multiplexer_1_out,
       multiplexer_2_out, multiplier_1_out, negator_1_out, or_1_out, or_2_out, shifter_1_out, shifter_2_out,
       shifter_3_out;

  Adder #(.width(16)) adder_1 (.a(op1), .b(op2), .out(adder_1_out));  // open: cin, cout
  Negator #(.width(16)) negator_1 (.in(op1), .out(negator_1_out));
  assign and_1_out = op1 & op2;  // AND_Gate and_1, 16 bits wide
  assign or_1_out = op1 | op2;  // OR_Gate or_1, 16 bits wide
  Multiplier #(.width(16)) multiplier_1 (.a(op1), .b(op2), .out(multiplier_1_out));  // open: cin, cout
  Adder #(.width(16)) adder_2 (.a(op1), .b({16{1'b0}}), .out(adder_2_out), .cout(adder_2_cout));  // open: cin
  Adder #(.width(16)) adder_3 (.a(op1), .b(op2), .out(adder_3_out), .cin(adder_2_cout));  // open: cout
  assign and_2_out = op1 & op2;  // AND_Gate and_2, 16 bits wide
  assign or_2_out = op1 | op2;  // OR_Gate or_2, 16 bits wide
  Shifter #(.width(16)) shifter_1 (.in(op1), .\dist (op2[3:0]), .out(shifter_1_out));
  Shifter #(.width(16), .shift("lr")) shifter_2 (.in(op1), .\dist (op2[3:0]), .out(shifter_2_out));
  Shifter #(.width(16), .shift("ar")) shifter_3 (.in(op1), .\dist (op2[3:0]), .out(shifter_3_out));
  Multiplexer #(.width(16)) multiplexer_1 (
    .in0(op1), .in1(op2), .out(multiplexer_1_out), .sel(comparator_1_lt));  // open: en
  Comparator #(.width(16)) comparator_1 (.a(op1), .b(op2), .lt(comparator_1_lt));  // open: gt, eq
  Multiplexer #(.width(16)) multiplexer_2 (
    .in0(op1), .in1(op2), .out(multiplexer_2_out), .sel(comparator_2_gt));  // open: en
  Comparator #(.width(16)) comparator_2 (.a(op1), .b(op2), .gt(comparator_2_gt));  // open: eq, lt
  Multiplexer #(.select(5), .width(16)) multiplexer_3 (
    .in1(adder_1_out), .in2(negator_1_out), .in5(and_1_out), .in6(or_1_out), .in7(multiplier_1_out),
    .in10(adder_2_out), .in11(adder_3_out), .in12(and_2_out), .in13(or_2_out), .in14(shifter_1_out),
    .in15(shifter_2_out), .in16(shifter_3_out), .in17(multiplexer_1_out), .in18(multiplexer_2_out),
    .out(data_output), .sel(opcode_decide_which_instrusion_would_be_selected), .en(1'b1));  // open: in0, in3, in4, in8, in9, in19, in20, in21, in22, in23, in24, in25, in26, in27, in28, in29, in30, in31

  // Notes on the sheet:
  //   r1
  //   r2
  //   1.li
  //   2.add
  //   3.neg
  //   4.ble
  //   5.halt
  //   6.and
  //   7.or
  //   8.mult
  //   9.load
  //   10.store
  //   11.move
  //   12.addi 
  //   13.andi
  //   14.ori
  //   15.lsl
  //   16.lsr
  //   17.asr
  //   18.max
  //   19.min
  //   20.jump
  //   21. call
  //   22.rtn
endmodule

module register (
  input  allow_write,
  input  [2:0] Read_Regisiter1,
  input  [2:0] Write_Register_which_reg,
  input  [2:0] Read_Regisiter2,
  input  reset,
  input  [15:0] Register_Data_data_input,
  input  clock_update_reg_per_clock,
  output [15:0] data_1,
  output [15:0] data_2
);

  wire and_1_out, and_2_out, and_3_out, and_4_out, and_5_out, and_6_out, and_7_out, and_8_out,
       decoder_1_out0, decoder_1_out1, decoder_1_out2, decoder_1_out3, decoder_1_out4, decoder_1_out5,
       decoder_1_out6, decoder_1_out7;
  wire [15:0] register_1_q, register_2_q, register_3_q, register_4_q, register_5_q, register_6_q,
       register_7_q, register_8_q;

  Decoder #(.select(3), .enable("false")) decoder_1 (
    .out0(decoder_1_out0), .out1(decoder_1_out1), .out2(decoder_1_out2), .out3(decoder_1_out3),
    .out4(decoder_1_out4), .out5(decoder_1_out5), .out6(decoder_1_out6), .out7(decoder_1_out7),
    .sel(Write_Register_which_reg));
  and and_1 (and_1_out, allow_write, decoder_1_out0);
  and and_2 (and_2_out, allow_write, decoder_1_out1);
  and and_3 (and_3_out, allow_write, decoder_1_out2);
  and and_4 (and_4_out, allow_write, decoder_1_out3);
  and and_5 (and_5_out, allow_write, decoder_1_out4);
  and and_6 (and_6_out, allow_write, decoder_1_out5);
  and and_7 (and_7_out, allow_write, decoder_1_out6);
  and and_8 (and_8_out, allow_write, decoder_1_out7);
  Register #(.width(16)) register_1 (
    .D(Register_Data_data_input), .en(and_1_out), .Q(register_1_q), .clk(clock_update_reg_per_clock),
    .clr(reset));
  Register #(.width(16)) register_2 (
    .D(Register_Data_data_input), .en(and_2_out), .Q(register_2_q), .clk(clock_update_reg_per_clock),
    .clr(reset));
  Register #(.width(16)) register_3 (
    .D(Register_Data_data_input), .en(and_3_out), .Q(register_3_q), .clk(clock_update_reg_per_clock),
    .clr(reset));
  Register #(.width(16)) register_4 (
    .D(Register_Data_data_input), .en(and_4_out), .Q(register_4_q), .clk(clock_update_reg_per_clock),
    .clr(reset));
  Register #(.width(16)) register_5 (
    .D(Register_Data_data_input), .en(and_5_out), .Q(register_5_q), .clk(clock_update_reg_per_clock),
    .clr(reset));
  Register #(.width(16)) register_6 (
    .D(Register_Data_data_input), .en(and_6_out), .Q(register_6_q), .clk(clock_update_reg_per_clock),
    .clr(reset));
  Register #(.width(16)) register_7 (
    .D(Register_Data_data_input), .en(and_7_out), .Q(register_7_q), .clk(clock_update_reg_per_clock),
    .clr(reset));
  Register #(.width(16)) register_8 (
    .D(Register_Data_data_input), .en(and_8_out), .Q(register_8_q), .clk(clock_update_reg_per_clock),
    .clr(reset));
  Multiplexer #(.select(3), .width(16), .enable("false")) multiplexer_1 (
    .in0(register_1_q), .in1(register_2_q), .in2(register_3_q), .in3(register_4_q), .in4(register_5_q),
    .in5(register_6_q), .in6(register_7_q), .in7(register_8_q), .out(data_1), .sel(Read_Regisiter1));
  Multiplexer #(.select(3), .width(16), .enable("false")) multiplexer_2 (
    .in0(register_1_q), .in1(register_2_q), .in2(register_3_q), .in3(register_4_q), .in4(register_5_q),
    .in5(register_6_q), .in6(register_7_q), .in7(register_8_q), .out(data_2), .sel(Read_Regisiter2));
endmodule

module control (
  input  [4:0] opcode,
  output shut_down_halt,
  output out_3,
  output write,
  output BLE,
  output I_or_R,
  output jump_cmd,
  output call,
  output rtn,
  output load_cmd,
  output store_cmd
);

  wire _2_out, _3_out, _6_out, _7_out, _8_out, _11_out, _12_out, _13_out, _14_out, _15_out, _16_out, _17_out,
       _18_out, _19_out, _20_out, _23_out, or_1_out;

  and _1 (out_3, ~opcode[4], ~opcode[3], ~opcode[2], ~opcode[1], ~opcode[0]);  // AND_Gate
  and _2 (_2_out, ~opcode[4], ~opcode[3], ~opcode[2], ~opcode[1], opcode[0]);  // AND_Gate
  and _3 (_3_out, ~opcode[4], ~opcode[3], ~opcode[2], opcode[1], ~opcode[0]);  // AND_Gate
  and _4 (BLE, ~opcode[4], ~opcode[3], ~opcode[2], opcode[1], opcode[0]);  // AND_Gate
  and _5 (shut_down_halt, ~opcode[4], ~opcode[3], opcode[2], ~opcode[1], ~opcode[0]);  // AND_Gate
  and _6 (_6_out, ~opcode[4], ~opcode[3], opcode[2], ~opcode[1], opcode[0]);  // AND_Gate
  and _7 (_7_out, ~opcode[4], ~opcode[3], opcode[2], opcode[1], ~opcode[0]);  // AND_Gate
  and _8 (_8_out, ~opcode[4], ~opcode[3], opcode[2], opcode[1], opcode[0]);  // AND_Gate
  and _9 (load_cmd, ~opcode[4], opcode[3], ~opcode[2], ~opcode[1], ~opcode[0]);  // AND_Gate
  and _10 (store_cmd, ~opcode[4], opcode[3], ~opcode[2], ~opcode[1], opcode[0]);  // AND_Gate
  and _11 (_11_out, ~opcode[4], opcode[3], ~opcode[2], opcode[1], ~opcode[0]);  // AND_Gate
  and _12 (_12_out, ~opcode[4], opcode[3], ~opcode[2], opcode[1], opcode[0]);  // AND_Gate
  and _13 (_13_out, ~opcode[4], opcode[3], opcode[2], ~opcode[1], ~opcode[0]);  // AND_Gate
  and _14 (_14_out, ~opcode[4], opcode[3], opcode[2], ~opcode[1], opcode[0]);  // AND_Gate
  and _15 (_15_out, ~opcode[4], opcode[3], opcode[2], opcode[1], ~opcode[0]);  // AND_Gate
  and _16 (_16_out, ~opcode[4], opcode[3], opcode[2], opcode[1], opcode[0]);  // AND_Gate
  and _17 (_17_out, opcode[4], ~opcode[3], ~opcode[2], ~opcode[1], ~opcode[0]);  // AND_Gate
  and _18 (_18_out, opcode[4], ~opcode[3], ~opcode[2], ~opcode[1], opcode[0]);  // AND_Gate
  and _19 (_19_out, opcode[4], ~opcode[3], ~opcode[2], opcode[1], ~opcode[0]);  // AND_Gate
  and _20 (_20_out, opcode[4], ~opcode[3], ~opcode[2], opcode[1], opcode[0]);  // AND_Gate
  and _21 (call, opcode[4], ~opcode[3], opcode[2], ~opcode[1], ~opcode[0]);  // AND_Gate
  and _22 (rtn, opcode[4], ~opcode[3], opcode[2], ~opcode[1], opcode[0]);  // AND_Gate
  and _23 (_23_out, opcode[4], ~opcode[3], opcode[2], opcode[1], ~opcode[0]);  // AND_Gate
  or or_1 (or_1_out, _20_out, BLE, store_cmd, call, rtn);
  not not_1 (write, or_1_out);
  or or_2 (I_or_R, _2_out, _3_out, _6_out, _7_out, _8_out, _11_out, _15_out, _16_out, _17_out, _18_out, _19_out);
  or or_3 (jump_cmd, _20_out, call);

  // Other names for the same wires on the sheet: _0 = opcode[0]; _1 = opcode[1]; _2 = opcode[2]; _3 = opcode[3];
  //   _4 = opcode[4]

  // Notes on the sheet:
  //   1.li
  //   2.add
  //   3.neg
  //   4.ble
  //   5.halt
  //   6.and
  //   7.or
  //   8.mult
  //   9.load
  //   10.store
  //   11.move
  //   12.addi 
  //   13.andi
  //   14.ori
  //   15.lsl
  //   16.lsr
  //   17.asr
  //   18.max
  //   19.min
  //   20.jump
  //   21. call
  //   22.rtn
  //   li instrusion?
  //   out 0 == I type ; 1== R type
endmodule
